# Fritzing sketch P3-Entrada_Analogica (saved by Fritzing 0.9.3b)
breadboards: 1

parts:
  U1 = ESP32-38PinWide [part_number=ESP32-38PinWide]
  R1 = Resistor [tolerance=±5% resistance=330 package=THT]
  LED1 = LED - 5mm [color="Yellow (595nm)" package="5 mm [THT]"]
  R2 = Resistor [tolerance=±5% resistance=330 package=THT]
  LED2 = LED - 5mm [color="Yellow (595nm)" package="5 mm [THT]"]
  R3 = Resistor [tolerance=±5% resistance=330 package=THT]
  R4 = Resistor [tolerance=±5% resistance=330 package=THT]
  LED3 = LED - 5mm [color="Green (570nm)" package="5 mm [THT]"]
  LED4 = LED - 5mm [color="Green (570nm)" package="5 mm [THT]"]
  R5 = Resistor [tolerance=±5% resistance=330 package=THT]
  LED5 = LED - 5mm [color="Red (633nm)" package="5 mm [THT]"]
  R6 = Resistor [tolerance=±5% resistance=330 package=THT]
  LED6 = LED - 5mm [color="Red (633nm)" package="5 mm [THT]"]
  R7 = Rotary Potentiometer (Small) [maximum_resistance=5kΩ package=THT]

nets:
  N1: U1.connector0, R7.leg2
  N2: U1.connector4, R7.wiper
  N3: U1.connector6, R4.Pin_1
  N4: U1.connector7, R3.Pin_1
  N5: U1.connector8, R2.Pin_1
  N6: U1.connector10, R1.Pin_1
  N7: U1.connector12, R5.Pin_1
  N8: U1.connector13, LED1.cathode, LED2.cathode, LED3.cathode, LED4.cathode, LED5.cathode, LED6.cathode, R7.leg1
  N9: U1.connector14, R6.Pin_1
  N10: R1.Pin_0, LED1.anode
  N11: R2.Pin_0, LED2.anode
  N12: R3.Pin_0, LED3.anode
  N13: R4.Pin_0, LED4.anode
  N14: R5.Pin_0, LED5.anode
  N15: R6.Pin_0, LED6.anode
